# Fritzing sketch Eureka_A4S_Esquematico (saved by Fritzing 0.8.7b)
breadboards: 1

parts:
  Componente1 = Arduino Uno (Rev3)
  S1 = Pushbutton [package="[THT]"]
  R1 = Resistor [tolerance=±5% resistance=1k package=THT]
  LED1 = LED - 5mm [color="Red (633nm)" package="5 mm [THT]"]
  R2 = Rotary Potentiometer (Small) [maximum_resistance=100kΩ package=THT]

nets:
  N1: Componente1.A0, R2.wiper
  N2: Componente1.D13/SCK, LED1.anode
  N3: Componente1.GND, R1.Pin_0, LED1.cathode, R2.leg1
  N4: Componente1.5V, S1.Pin_1, S1.Pin_2, R2.leg2
  N5: S1.Pin_3, S1.Pin_4, R1.Pin_1
